# Fritzing sketch OrionKart (saved by Fritzing 0.9.3b)
circuit board: 10cm x 10cm

parts:
  LED1 = LED - 5mm [color="Red (633nm)" package="5 mm [THT]"]
  FUNYE1 = SIP - 2 pins [chip_label=Funye package="SIP (Single Inline) [THT]"]
  BMP280 = GY-BMEP280 Barometric Pressure Sensor - Breakout
  LORA1 = IC, SIP package, 4 pins [chip_label=LORA]
  FUNYE = SIP - 2 pins [chip_label=Funye package="SIP (Single Inline) [THT]"]
  R2 = Resistor [tolerance=±5% resistance=220 package=THT]
  LED2 = LED - 5mm [color="Red (633nm)" package="5 mm [THT]"]
  L86 = IC, DIP package, 12 pins [chip_label=L86]
  R1 = Resistor [tolerance=±5% resistance=220 package=THT]
  BNO055 = 9-DOF Absolute Orientation IMU Fusion Breakout - BNO055
  SG1 = Buzzer 12mm [package=buzzer-12mm]
  MEGA_MINI1 = Mega2560 R3 Pro Mini
  Q3 = Basic FET N-Channel [package="TO220 [THT]"]
  Q4 = Basic FET N-Channel [package="TO220 [THT]"]
  T-C-M-1 = T-Connector Male [package=THT]

nets:
  N1: LED1.cathode, MEGA_MINI1.40
  N2: LED1.anode, R1.Pin_1
  N3: FUNYE1.pin1, BMP280.VCC, LORA1.pin1, FUNYE.pin1, BNO055.5.0V, MEGA_MINI1.GND-2, MEGA_MINI1.GND-3
  N4: FUNYE1.pin2, FUNYE.pin2, Q3.drain, Q4.drain
  GND: BMP280.GND, LORA1.pin2, R2.Pin_1, L86.pin3, R1.Pin_0, BNO055.GND, SG1.1, MEGA_MINI1.Vin-1, Q3.source, Q4.source, T-C-M-1.GND
  N5: BMP280.SCL, BNO055.SCL_5V, MEGA_MINI1.21
  N6: BMP280.SDA, BNO055.SDA_5V, MEGA_MINI1.20
  N7: LORA1.pin3, MEGA_MINI1.14
  N8: LORA1.pin4, MEGA_MINI1.15
  N9: R2.Pin_0, LED2.anode
  N10: LED2.cathode, MEGA_MINI1.42
  N11: L86.pin1, MEGA_MINI1.18
  N12: L86.pin2, MEGA_MINI1.19
  N13: L86.pin4, L86.pin5, MEGA_MINI1.VCC, MEGA_MINI1.5V-2, MEGA_MINI1.VTG
  N14: SG1.2, MEGA_MINI1.38
  N15: MEGA_MINI1.46, Q3.gate
  N16: MEGA_MINI1.44, Q4.gate

custom parts:
  GY-BMEP280 Barometric Pressure Sensor - Breakout: The BME280 is a chip which was originally designed for the next generation of smartphones. It is made up of a very accurate pressure sensor and an associated temperature sensor which helps calibrate the pressure readings. And just for fun they threw in a pretty solid humidity sensor in there as well! So with an I2C connection you have access to enough weather data to make some pretty good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
  9-DOF Absolute Orientation IMU Fusion Breakout - BNO055: A MEMS accelerometer, magnetometer and gyroscope on a single die with a high speed ARM Cortex-M0 based processor to digest all the sensor data, abstract the sensor fusion and real time requirements away, and spit out data you can use in quaternions, Euler angles or vectors.
  Mega2560 R3 Pro Mini: The Mega 2560 R3 Pro Mini :- Completely compatible with original Arduino Mega2560 Pin pitch: 0.1 inch Size: 5.42cm*3.68cm With Atmega16U2 chip as the USB to Serial converter 5V working voltage. Input Voltage:7-12V Analog Input Pins: 16 Digital I/O pins: 54 The Mega 2560 R3 Pro Mini has no datasheet and no info and I don't have one to compare, so I made this based on photos. Dec 2019 modified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
  T-Connector Male: Red T - Male Connector for high current loads up to 60A.
